// Logisim project computer.circ as structural Verilog: 1 circuit, main circuit main
module main (
);

  wire button_1_out, button_2_out, clock_1_out, mmu_1_mem_en, mmu_1_pia_en, mmu_1_vga_en, pia_1_io_write,
       pia_1_irq, riscv_core_1_mem_rd, riscv_core_1_mem_write, vga_1_sys_clk;
  wire [1:0] riscv_core_1_data_type;
  wire [7:0] bit_extender_1_out, keyboard_1_data, pia_1_io_read, pia_1_uart_tx, vga_1_blue, vga_1_green,
       vga_1_red;
  wire [9:0] vga_1_h_pos, vga_1_v_pos;
  wire [31:0] pia_1_data_out, riscv_core_1_address, riscv_core_1_data_out;

  // Probe on riscv_core_1_address
  riscv_core riscv_core_1 (
    .data_in(pia_1_data_out), .irq(pia_1_irq), .clk(vga_1_sys_clk), .reset(button_1_out),
    .data_out(riscv_core_1_data_out), .data_type(riscv_core_1_data_type), .mem_rd(riscv_core_1_mem_rd),
    .mem_write(riscv_core_1_mem_write), .address(riscv_core_1_address));
  // Probe on pia_1_data_out
  Button button_1 (.out(button_1_out));
  Button button_2 (.out(button_2_out));
  mmu mmu_1 (.address(riscv_core_1_address), .mem_en(mmu_1_mem_en), .vga_en(mmu_1_vga_en), .pia_en(mmu_1_pia_en));
  Clock clock_1 (.out(clock_1_out));
  assign bit_extender_1_out = {{7{button_2_out}}, button_2_out};  // Bit_Extender bit_extender_1
  pia pia_1 (
    .pia_write(riscv_core_1_mem_write), .en(mmu_1_pia_en), .clk(vga_1_sys_clk), .reset(button_1_out),
    .pia_read(riscv_core_1_mem_rd), .data_in(riscv_core_1_data_out), .address(riscv_core_1_address),
    .port_a_in(keyboard_1_data), .uart_rx(bit_extender_1_out), .io_read(pia_1_io_read),
    .uart_tx(pia_1_uart_tx), .io_write(pia_1_io_write), .irq(pia_1_irq), .data_out(pia_1_data_out));  // open: port_b_in, port_a_out, port_b_out
  single_ram_1Mx8 single_ram_1mx8_1 (
    .enable(mmu_1_mem_en), .ram_write(riscv_core_1_mem_write), .clk(vga_1_sys_clk),
    .data_type(riscv_core_1_data_type), .cpu_address(riscv_core_1_address), .data_in(riscv_core_1_data_out),
    .cpu_data_out(pia_1_data_out));
  vga vga_1 (
    .reset(button_1_out), .ctrl_en(mmu_1_vga_en), .ctrl_read(riscv_core_1_mem_rd), .clk(clock_1_out),
    .data_in(riscv_core_1_data_out), .cpu_address(riscv_core_1_address), .data_type(riscv_core_1_data_type),
    .write(riscv_core_1_mem_write), .ram_en(mmu_1_mem_en), .v_pos(vga_1_v_pos), .h_pos(vga_1_h_pos),
    .ctrl_out(pia_1_data_out), .red(vga_1_red), .green(vga_1_green), .blue(vga_1_blue),
    .sys_clk(vga_1_sys_clk));  // open: v_sync, h_sync
  // RGB_Video #(.height(64), .width(64)) rgb_video_1: pin names not known; wires that end beside it: button_1_out, vga_1_sys_clk, vga_1_sys_clk, vga_1_h_pos[5:0], vga_1_v_pos[5:0], {vga_1_red, vga_1_green, vga_1_blue}
  TTY tty_1 (.data(pia_1_uart_tx[6:0]), .clk(vga_1_sys_clk), .we(pia_1_io_write), .clr(button_1_out));
  Keyboard keyboard_1 (
    .clk(vga_1_sys_clk), .re(pia_1_io_read[0]), .clr(button_1_out), .avail(keyboard_1_data[7]),
    .data(keyboard_1_data[6:0]));
endmodule
