// Logisim project memory_mgmt.circ as structural Verilog: 1 circuit, main circuit mmu
module mmu (
  input  [31:0] address,
  output mem_en,
  output vga_en,
  output pia_en
);

  wire comparator_1_eq, comparator_1_gt, comparator_2_eq, comparator_2_lt, comparator_3_eq, comparator_3_gt,
       comparator_4_eq, comparator_4_lt, comparator_5_eq, comparator_5_gt, comparator_6_eq, comparator_6_lt,
       or_1_out, or_2_out, or_3_out, or_4_out, or_5_out, or_6_out;

  Comparator #(.mode("unsigned"), .width(20)) comparator_1 (
    .a(address[19:0]), .b({20{1'b0}}), .gt(comparator_1_gt), .eq(comparator_1_eq));  // open: lt
  Comparator #(.mode("unsigned"), .width(20)) comparator_2 (
    .a(address[19:0]), .b(20'heffff), .eq(comparator_2_eq), .lt(comparator_2_lt));  // open: gt
  Comparator #(.mode("unsigned"), .width(20)) comparator_3 (
    .a(address[19:0]), .b(20'hfff00), .gt(comparator_3_gt), .eq(comparator_3_eq));  // open: lt
  Comparator #(.mode("unsigned"), .width(20)) comparator_4 (
    .a(address[19:0]), .b(20'hfff20), .eq(comparator_4_eq), .lt(comparator_4_lt));  // open: gt
  Comparator #(.mode("unsigned"), .width(20)) comparator_5 (
    .a(address[19:0]), .b(20'hffff0), .gt(comparator_5_gt), .eq(comparator_5_eq));  // open: lt
  Comparator #(.mode("unsigned"), .width(20)) comparator_6 (
    .a(address[19:0]), .b({20{1'b1}}), .eq(comparator_6_eq), .lt(comparator_6_lt));  // open: gt
  or or_1 (or_1_out, comparator_1_gt, comparator_1_eq);
  or or_2 (or_2_out, comparator_2_eq, comparator_2_lt);
  or or_3 (or_3_out, comparator_3_gt, comparator_3_eq);
  or or_4 (or_4_out, comparator_4_eq, comparator_4_lt);
  or or_5 (or_5_out, comparator_5_gt, comparator_5_eq);
  or or_6 (or_6_out, comparator_6_eq, comparator_6_lt);
  and and_1 (mem_en, or_1_out, or_2_out);
  and and_2 (vga_en, or_3_out, or_4_out);
  and and_3 (pia_en, or_5_out, or_6_out);

  // Notes on the sheet:
  //   MEM
  //   VGA
  //   PIA
endmodule
