// Logisim project peripheral_interface.circ as structural Verilog: 8 circuits, main circuit pia
module pia (
  input  [31:0] data_in,
  input  [7:0] port_a_in,
  input  [7:0] port_b_in,
  input  [7:0] uart_rx,
  input  clk,
  input  reset,
  input  pia_write,
  input  en,
  input  [31:0] address,
  input  pia_read,
  output [7:0] port_a_out,
  output [7:0] port_b_out,
  output [7:0] uart_tx,
  output [31:0] data_out,
  output irq,
  output io_write,
  output [7:0] io_read
);

  wire and_1_out, and_3_out, decoder_1_out0, decoder_1_out1, decoder_1_out2, decoder_1_out3, decoder_1_out4,
       decoder_1_out5, decoder_1_out6, not_1_out;
  wire [7:0] bit_extender_1_out, decoder_2_out0;
  wire [31:0] io_reg_1_data_dir_out, io_reg_1_port_data, io_reg_2_data_dir_out, io_reg_2_port_data,
       irq_control_v2_1_irq_en, irq_control_v2_1_irq_vector, multiplexer_1_out, register_1_q,
       uart_control_1_uart_rx_out;

  not not_1 (not_1_out, clk);
  and and_1 (and_1_out, pia_write, en);
  Decoder #(.select(3)) decoder_1 (
    .out0(decoder_1_out0), .out1(decoder_1_out1), .out2(decoder_1_out2), .out3(decoder_1_out3),
    .out4(decoder_1_out4), .out5(decoder_1_out5), .out6(decoder_1_out6), .sel(address[2:0]), .en(and_1_out));  // open: out7
  and and_2 (io_write, ~decoder_1_out5, ~decoder_1_out6, and_1_out);  // AND_Gate
  and and_3 (and_3_out, ~decoder_1_out5, ~decoder_1_out6, en, pia_read);  // AND_Gate
  io_reg io_reg_1 (
    .data_dir_load(decoder_1_out1), .port_out_load(decoder_1_out0), .clk(not_1_out), .reset(reset),
    .data_in(data_in[7:0]), .port_in(port_a_in), .data_dir_out(io_reg_1_data_dir_out), .port_out(port_a_out),
    .port_data(io_reg_1_port_data));
  io_reg io_reg_2 (
    .data_dir_load(decoder_1_out3), .port_out_load(decoder_1_out2), .clk(not_1_out), .reset(reset),
    .data_in(data_in[7:0]), .port_in(port_b_in), .data_dir_out(io_reg_2_data_dir_out), .port_out(port_b_out),
    .port_data(io_reg_2_port_data));
  uart_control uart_control_1 (
    .uart_tx_en(decoder_1_out4), .clk(not_1_out), .reset(reset), .uart_rx_in(uart_rx),
    .uart_tx_in(data_in[7:0]), .uart_tx_out(uart_tx), .uart_rx_out(uart_control_1_uart_rx_out));
  irq_control_v2 irq_control_v2_1 (
    .irq_handle_en(decoder_1_out6), .irq_en_wr(decoder_1_out5), .clk(not_1_out), .reset(reset),
    .ddra(io_reg_1_data_dir_out), .ddrb(io_reg_2_data_dir_out), .data_in(data_in), .port_a_in(port_a_in),
    .port_b_in(port_b_in), .uart_rx(uart_rx), .irq(irq), .irq_en(irq_control_v2_1_irq_en),
    .irq_vector(irq_control_v2_1_irq_vector));
  Multiplexer #(.select(3), .width(32)) multiplexer_1 (
    .in0(io_reg_1_port_data), .in1(io_reg_1_data_dir_out), .in2(io_reg_2_port_data),
    .in3(io_reg_2_data_dir_out), .in4(uart_control_1_uart_rx_out), .in5(irq_control_v2_1_irq_en),
    .in6(irq_control_v2_1_irq_vector), .out(multiplexer_1_out), .sel(address[2:0]));  // open: in7
  Decoder #(.enable("false"), .select(3)) decoder_2 (
    .out0(decoder_2_out0[0]), .out1(decoder_2_out0[1]), .out2(decoder_2_out0[2]), .out3(decoder_2_out0[3]),
    .out4(decoder_2_out0[4]), .out5(decoder_2_out0[5]), .out6(decoder_2_out0[6]), .out7(decoder_2_out0[7]),
    .sel(address[2:0]));
  Register #(.width(32)) register_1 (
    .D(multiplexer_1_out), .en(and_3_out), .clk(not_1_out), .Q(register_1_q), .clr(reset));
  assign data_out = and_3_out ? register_1_q : 32'bz;  // Controlled_Buffer controlled_buffer_1
  assign bit_extender_1_out = {{7{1'b1}}, and_3_out};  // Bit_Extender bit_extender_1
  assign io_read = bit_extender_1_out & decoder_2_out0;  // AND_Gate and_4, 8 bits wide
endmodule

module io_reg (
  input  [7:0] data_in,
  input  data_dir_load,
  input  port_out_load,
  input  clk,
  input  reset,
  input  [7:0] port_in,
  output [31:0] data_dir_out,
  output [7:0] port_out,
  output [31:0] port_data
);

  wire [7:0] controlled_buffer_8bit_1_data_out, not_1_out, register_1_q, register_2_q;

  Register register_1 (.D(data_in), .en(data_dir_load), .clk(clk), .Q(register_1_q), .clr(reset));
  Register register_2 (.D(data_in), .en(port_out_load), .clk(clk), .Q(register_2_q), .clr(reset));
  assign not_1_out = ~register_1_q;  // NOT_Gate not_1, 8 bits wide
  controlled_buffer_8bit controlled_buffer_8bit_1 (
    .data_en(not_1_out), .data_in(port_in), .data_out(controlled_buffer_8bit_1_data_out));
  assign data_dir_out = {{24{1'b0}}, register_1_q};  // Bit_Extender bit_extender_1
  controlled_buffer_8bit controlled_buffer_8bit_2 (.data_en(register_1_q), .data_in(register_2_q), .data_out(port_out));
  assign port_data = {{24{controlled_buffer_8bit_1_data_out[7]}}, controlled_buffer_8bit_1_data_out};  // Bit_Extender bit_extender_2
endmodule

module controlled_buffer_8bit (
  input  [7:0] data_en,
  input  [7:0] data_in,
  output [7:0] data_out
);

  assign data_out[6] = data_en[6] ? data_in[6] : 1'bz;  // Controlled_Buffer controlled_buffer_1
  assign data_out[7] = data_en[7] ? data_in[7] : 1'bz;  // Controlled_Buffer controlled_buffer_2
  assign data_out[2] = data_en[2] ? data_in[2] : 1'bz;  // Controlled_Buffer controlled_buffer_3
  assign data_out[3] = data_en[3] ? data_in[3] : 1'bz;  // Controlled_Buffer controlled_buffer_4
  assign data_out[4] = data_en[4] ? data_in[4] : 1'bz;  // Controlled_Buffer controlled_buffer_5
  assign data_out[5] = data_en[5] ? data_in[5] : 1'bz;  // Controlled_Buffer controlled_buffer_6
  assign data_out[0] = data_en[0] ? data_in[0] : 1'bz;  // Controlled_Buffer controlled_buffer_7
  assign data_out[1] = data_en[1] ? data_in[1] : 1'bz;  // Controlled_Buffer controlled_buffer_8
endmodule

module irq_vector_generator (
  input  [7:0] port_a_in,
  input  [31:0] ddra,
  input  [7:0] port_b_in,
  input  [31:0] ddrb,
  input  [7:0] uart_rx,
  input  clk,
  input  reset,
  output [31:0] irq_vector,
  output irq
);

  wire comparator_1_eq, comparator_2_eq, comparator_3_eq, or_1_out;
  wire [7:0] and_1_out, and_2_out, register_1_q, register_2_q, register_3_q, xor_1_out, xor_2_out, xor_3_out;

  assign and_1_out = port_a_in & ~ddra[7:0];  // AND_Gate and_1, 8 bits wide
  assign and_2_out = port_b_in & ~ddrb[7:0];  // AND_Gate and_2, 8 bits wide
  Register #(.trigger("falling")) register_1 (.D(and_1_out), .en(1'b1), .clk(clk), .Q(register_1_q), .clr(reset));
  Register #(.trigger("falling")) register_2 (.D(and_2_out), .en(1'b1), .clk(clk), .Q(register_2_q), .clr(reset));
  Register #(.trigger("falling")) register_3 (.D(uart_rx), .en(1'b1), .clk(clk), .Q(register_3_q), .clr(reset));
  assign xor_1_out = and_1_out ^ register_1_q;  // XOR_Gate xor_1, 8 bits wide
  assign xor_2_out = and_2_out ^ register_2_q;  // XOR_Gate xor_2, 8 bits wide
  assign xor_3_out = uart_rx ^ register_3_q;  // XOR_Gate xor_3, 8 bits wide
  not not_1 (irq_vector[0], comparator_1_eq);
  Comparator #(.mode("unsigned")) comparator_1 (.a(xor_1_out), .b({8{1'b0}}), .eq(comparator_1_eq));  // open: gt, lt
  not not_2 (irq_vector[1], comparator_2_eq);
  Comparator #(.mode("unsigned")) comparator_2 (.a(xor_2_out), .b({8{1'b0}}), .eq(comparator_2_eq));  // open: gt, lt
  not not_3 (irq_vector[2], comparator_3_eq);
  Comparator #(.mode("unsigned")) comparator_3 (.a(xor_3_out), .b({8{1'b0}}), .eq(comparator_3_eq));  // open: gt, lt
  D_Flip_Flop d_ff_1 (.D(or_1_out), .clk(clk), .Q(irq), .reset(reset));  // open: Qn, preset
  or or_1 (or_1_out, irq_vector[0], irq_vector[1], irq_vector[2]);

  assign irq_vector[31:3] = {29{1'b0}};
endmodule

module uart_control (
  input  [7:0] uart_rx_in,
  input  [7:0] uart_tx_in,
  input  uart_tx_en,
  input  clk,
  input  reset,
  output [31:0] uart_rx_out,
  output [7:0] uart_tx_out
);

  assign uart_rx_out = {{24{uart_rx_in[7]}}, uart_rx_in};  // Bit_Extender bit_extender_1
  Register register_1 (.D(uart_tx_in), .en(uart_tx_en), .clk(clk), .Q(uart_tx_out), .clr(reset));
endmodule

module irq_control (
  input  [7:0] port_a_in,
  input  [31:0] ddra,
  input  [7:0] port_b_in,
  input  [31:0] ddrb,
  input  [7:0] uart_rx,
  input  irq_handle_en,
  input  [31:0] data_in,
  input  irq_en_wr,
  input  isr_location_wr,
  input  [31:0] pc_in,
  input  clk,
  input  reset,
  output [31:0] irq_vector,
  output irq,
  output [31:0] irq_en,
  output [31:0] isr_location,
  output pc_en,
  output [31:0] pc_out
);

  wire and_3_out, d_ff_1_q, or_1_out, or_2_out, register_1_q;
  wire [7:0] and_1_out, and_2_out;
  wire [31:0] register_3_q;

  assign and_1_out = port_a_in & ~ddra[7:0];  // AND_Gate and_1, 8 bits wide
  assign and_2_out = port_b_in & ~ddrb[7:0];  // AND_Gate and_2, 8 bits wide
  and and_3 (and_3_out, irq_handle_en, data_in[0]);
  or or_1 (or_1_out, reset, and_3_out);
  Register #(.width(1)) register_1 (.D(data_in[0]), .en(irq_en_wr), .clk(clk), .Q(register_1_q), .clr(reset));
  Register #(.width(32)) register_2 (.D(data_in), .en(isr_location_wr), .clk(clk), .Q(isr_location), .clr(reset));
  Register #(.width(32)) register_3 (.D(pc_in), .en(pc_en), .clk(clk), .Q(register_3_q), .clr(reset));
  sr_latch_8_bit sr_latch_8_bit_1 (.irq_handle(or_1_out), .port_in(and_1_out), .change_detected(irq_vector[0]));
  sr_latch_8_bit sr_latch_8_bit_2 (.irq_handle(or_1_out), .port_in(and_2_out), .change_detected(irq_vector[1]));
  sr_latch_8_bit sr_latch_8_bit_3 (.irq_handle(or_1_out), .port_in(uart_rx), .change_detected(irq_vector[2]));
  D_Flip_Flop d_ff_1 (.D(irq), .clk(clk), .Q(d_ff_1_q), .reset(or_1_out));  // open: Qn, preset
  or or_2 (or_2_out, irq_vector[0], irq_vector[1], irq_vector[2]);
  assign irq_en = {{31{1'b0}}, register_1_q};  // Bit_Extender bit_extender_1
  and and_4 (irq, or_2_out, register_1_q);
  and and_5 (pc_en, irq, ~d_ff_1_q);  // AND_Gate
  Multiplexer #(.width(32)) multiplexer_1 (.in0(register_3_q), .in1(isr_location), .out(pc_out), .sel(irq));

  assign irq_vector[31:3] = {29{1'b0}};
endmodule

module sr_latch_8_bit (
  input  [7:0] port_in,
  input  irq_handle,
  output change_detected
);

  wire and_1_out, and_2_out, and_3_out, and_4_out, and_5_out, and_6_out, and_7_out, and_8_out, s_r_ff_1_q,
       s_r_ff_2_q, s_r_ff_3_q, s_r_ff_4_q, s_r_ff_5_q, s_r_ff_6_q, s_r_ff_7_q, s_r_ff_8_q, s_r_ff_9_q,
       s_r_ff_10_q, s_r_ff_11_q, s_r_ff_12_q, s_r_ff_13_q, s_r_ff_14_q, s_r_ff_15_q, s_r_ff_16_q;
  wire [7:0] not_1_out;

  S_R_Flip_Flop s_r_ff_1 (.Q(s_r_ff_1_q), .reset(irq_handle), .preset(port_in[7]));  // open: S, R, clk, Qn
  assign not_1_out = ~port_in;  // NOT_Gate not_1, 8 bits wide
  S_R_Flip_Flop s_r_ff_2 (.Q(s_r_ff_2_q), .reset(irq_handle), .preset(not_1_out[7]));  // open: S, R, clk, Qn
  S_R_Flip_Flop s_r_ff_3 (.Q(s_r_ff_3_q), .reset(irq_handle), .preset(port_in[6]));  // open: S, R, clk, Qn
  S_R_Flip_Flop s_r_ff_4 (.Q(s_r_ff_4_q), .reset(irq_handle), .preset(not_1_out[6]));  // open: S, R, clk, Qn
  and and_1 (and_1_out, s_r_ff_2_q, s_r_ff_1_q);
  and and_2 (and_2_out, s_r_ff_4_q, s_r_ff_3_q);
  S_R_Flip_Flop s_r_ff_5 (.Q(s_r_ff_5_q), .reset(irq_handle), .preset(port_in[5]));  // open: S, R, clk, Qn
  S_R_Flip_Flop s_r_ff_6 (.Q(s_r_ff_6_q), .reset(irq_handle), .preset(not_1_out[5]));  // open: S, R, clk, Qn
  and and_3 (and_3_out, s_r_ff_6_q, s_r_ff_5_q);
  S_R_Flip_Flop s_r_ff_7 (.Q(s_r_ff_7_q), .reset(irq_handle), .preset(port_in[4]));  // open: S, R, clk, Qn
  S_R_Flip_Flop s_r_ff_8 (.Q(s_r_ff_8_q), .reset(irq_handle), .preset(not_1_out[4]));  // open: S, R, clk, Qn
  and and_4 (and_4_out, s_r_ff_8_q, s_r_ff_7_q);
  S_R_Flip_Flop s_r_ff_9 (.Q(s_r_ff_9_q), .reset(irq_handle), .preset(port_in[3]));  // open: S, R, clk, Qn
  S_R_Flip_Flop s_r_ff_10 (.Q(s_r_ff_10_q), .reset(irq_handle), .preset(not_1_out[3]));  // open: S, R, clk, Qn
  or or_1 (change_detected, and_1_out, and_2_out, and_3_out, and_4_out, and_5_out, and_6_out, and_7_out, and_8_out);
  S_R_Flip_Flop s_r_ff_11 (.Q(s_r_ff_11_q), .reset(irq_handle), .preset(port_in[2]));  // open: S, R, clk, Qn
  S_R_Flip_Flop s_r_ff_12 (.Q(s_r_ff_12_q), .reset(irq_handle), .preset(not_1_out[2]));  // open: S, R, clk, Qn
  and and_5 (and_5_out, s_r_ff_10_q, s_r_ff_9_q);
  S_R_Flip_Flop s_r_ff_13 (.Q(s_r_ff_13_q), .reset(irq_handle), .preset(port_in[1]));  // open: S, R, clk, Qn
  S_R_Flip_Flop s_r_ff_14 (.Q(s_r_ff_14_q), .reset(irq_handle), .preset(not_1_out[1]));  // open: S, R, clk, Qn
  and and_6 (and_6_out, s_r_ff_12_q, s_r_ff_11_q);
  S_R_Flip_Flop s_r_ff_15 (.Q(s_r_ff_15_q), .reset(irq_handle), .preset(port_in[0]));  // open: S, R, clk, Qn
  S_R_Flip_Flop s_r_ff_16 (.Q(s_r_ff_16_q), .reset(irq_handle), .preset(not_1_out[0]));  // open: S, R, clk, Qn
  and and_7 (and_7_out, s_r_ff_14_q, s_r_ff_13_q);
  and and_8 (and_8_out, s_r_ff_16_q, s_r_ff_15_q);
endmodule

module irq_control_v2 (
  input  [7:0] port_a_in,
  input  [31:0] ddra,
  input  [7:0] port_b_in,
  input  [31:0] ddrb,
  input  [7:0] uart_rx,
  input  irq_handle_en,
  input  [31:0] data_in,
  input  irq_en_wr,
  input  clk,
  input  reset,
  output [31:0] irq_vector,
  output irq,
  output [31:0] irq_en
);

  wire and_3_out, or_1_out, or_2_out, register_1_q;
  wire [7:0] and_1_out, and_2_out;

  assign and_1_out = port_a_in & ~ddra[7:0];  // AND_Gate and_1, 8 bits wide
  assign and_2_out = port_b_in & ~ddrb[7:0];  // AND_Gate and_2, 8 bits wide
  and and_3 (and_3_out, irq_handle_en, data_in[0]);
  or or_1 (or_1_out, reset, and_3_out);
  Register #(.width(1)) register_1 (.D(data_in[0]), .en(irq_en_wr), .clk(clk), .Q(register_1_q), .clr(reset));
  sr_latch_8_bit sr_latch_8_bit_1 (.irq_handle(or_1_out), .port_in(and_1_out), .change_detected(irq_vector[0]));
  sr_latch_8_bit sr_latch_8_bit_2 (.irq_handle(or_1_out), .port_in(and_2_out), .change_detected(irq_vector[1]));
  sr_latch_8_bit sr_latch_8_bit_3 (.irq_handle(or_1_out), .port_in(uart_rx), .change_detected(irq_vector[2]));
  or or_2 (or_2_out, irq_vector[0], irq_vector[1], irq_vector[2]);
  assign irq_en = {{31{1'b0}}, register_1_q};  // Bit_Extender bit_extender_1
  and and_4 (irq, or_2_out, register_1_q);

  assign irq_vector[31:3] = {29{1'b0}};
endmodule
