// Logisim project ram.circ as structural Verilog: 4 circuits, main circuit dual_ram_1Mx8
module dual_ram_1Mx8 (
  input  [31:0] cpu_address,
  input  [31:0] data_in,
  input  enable,
  input  ram_write,
  input  reset,
  input  clk,
  input  [1:0] data_type,
  input  [31:0] vga_address,
  output sys_clk,
  output [31:0] cpu_data_out,
  output [31:0] vga_data_out
);

  wire and_1_out, not_1_out, or_1_out, ram_clk_gen_1_ram_clk, ram_clk_gen_1_ram_write;
  wire [7:0] ram_1_p7, ram_1_p8, ram_1_p9, ram_1_p10, ram_2_p7, ram_2_p8, ram_2_p9, ram_2_p10;
  wire [31:0] multiplexer_1_out, register_1_q;

  ram_clk_gen ram_clk_gen_1 (
    .reset(reset), .clk(clk), .ram_clk(ram_clk_gen_1_ram_clk), .ram_write(ram_clk_gen_1_ram_write),
    .sys_clk(sys_clk));
  or or_1 (or_1_out, data_type[0], data_type[1]);
  and and_1 (and_1_out, enable, ram_write, ram_clk_gen_1_ram_write);
  Multiplexer #(.width(32)) multiplexer_1 (
    .in0(vga_address), .in1(cpu_address), .out(multiplexer_1_out), .sel(and_1_out));
  // RAM #(.addrWidth(20), .enables("line"), .line("quad"), .misaligned("true"), .trigger("falling"), .\type ("nonvolatile")) ram_1: pin names not known; wires that end beside it: and_1_out, 1'b1, or_1_out, data_type[1], data_type[1], ram_clk_gen_1_ram_clk, ram_1_p7, ram_1_p8, ram_1_p9, ram_1_p10
  // RAM #(.addrWidth(20), .enables("line"), .line("quad"), .misaligned("true"), .trigger("falling"), .\type ("nonvolatile")) ram_2: pin names not known; wires that end beside it: and_1_out, 1'b1, or_1_out, data_type[1], data_type[1], ram_clk_gen_1_ram_clk, ram_2_p7, ram_2_p8, ram_2_p9, ram_2_p10
  not not_1 (not_1_out, and_1_out);
  Register #(.width(32)) register_1 (
    .D({ram_1_p10, ram_1_p9, ram_1_p8, ram_1_p7}), .en(not_1_out), .clk(ram_clk_gen_1_ram_clk),
    .Q(register_1_q), .clr(reset));
  Register #(.width(32)) register_2 (
    .D({ram_2_p10, ram_2_p9, ram_2_p8, ram_2_p7}), .en(not_1_out), .clk(ram_clk_gen_1_ram_clk),
    .Q(vga_data_out), .clr(reset));
  assign cpu_data_out = enable ? register_1_q : 32'bz;  // Controlled_Buffer controlled_buffer_1
endmodule

module ram_clk_gen (
  input  reset,
  input  clk,
  output ram_write,
  output sys_clk,
  output ram_clk
);

  Counter #(.max('h1), .width(1)) counter_1 (
    .clr(reset), .load(1'b0), .up(1'b1), .count(1'b1), .clk(clk), .carry(ram_write));  // open: D, Q
  not not_1 (sys_clk, ram_write);

  assign ram_clk = clk;
endmodule

module single_ram_1Mx8 (
  input  [31:0] cpu_address,
  input  [31:0] data_in,
  input  enable,
  input  ram_write,
  input  [1:0] data_type,
  input  clk,
  output [31:0] cpu_data_out
);

  wire and_1_out, or_1_out;
  wire [7:0] ram_1_p7, ram_1_p8, ram_1_p9, ram_1_p10;

  and and_1 (and_1_out, enable, ram_write);
  or or_1 (or_1_out, data_type[0], data_type[1]);
  // RAM #(.addrWidth(20), .enables("line"), .line("quad"), .misaligned("true"), .trigger("falling"), .\type ("nonvolatile")) ram_1: pin names not known; wires that end beside it: and_1_out, 1'b1, or_1_out, data_type[1], data_type[1], clk, ram_1_p7, ram_1_p8, ram_1_p9, ram_1_p10
  assign cpu_data_out = enable ? {ram_1_p10, ram_1_p9, ram_1_p8, ram_1_p7} : 32'bz;  // Controlled_Buffer controlled_buffer_1
endmodule

module vga_mem (
  input  [31:0] vga_address,
  input  [31:0] cpu_address,
  input  enable,
  input  ram_write,
  input  reset,
  input  clk,
  input  [31:0] data_in,
  input  [1:0] data_type,
  input  [31:0] color_fg_address,
  input  [31:0] color_bg_address,
  input  [31:0] character_rom_address,
  output sys_clk,
  output [31:0] vga_data_out,
  output [31:0] color_fg_out,
  output [31:0] color_bg_out,
  output [31:0] character_data
);

  wire and_1_out, not_1_out, or_1_out, ram_clk_gen_1_ram_clk, ram_clk_gen_1_ram_write;
  wire [7:0] ram_1_p8, ram_1_p9, ram_1_p10, ram_1_p11, ram_2_p8, ram_2_p9, ram_2_p10, ram_2_p11, ram_3_p8,
       ram_3_p9, ram_3_p10, ram_3_p11, ram_4_p8, ram_4_p9, ram_4_p10, ram_4_p11;
  wire [31:0] multiplexer_1_out, multiplexer_2_out, multiplexer_3_out, multiplexer_4_out;

  and and_1 (and_1_out, enable, ram_write, ram_clk_gen_1_ram_write);
  ram_clk_gen ram_clk_gen_1 (
    .reset(reset), .clk(clk), .ram_clk(ram_clk_gen_1_ram_clk), .ram_write(ram_clk_gen_1_ram_write),
    .sys_clk(sys_clk));
  or or_1 (or_1_out, data_type[0], data_type[1]);
  Multiplexer #(.width(32)) multiplexer_1 (
    .in0(vga_address), .in1(cpu_address), .out(multiplexer_1_out), .sel(and_1_out));
  Multiplexer #(.width(32)) multiplexer_2 (
    .in0(color_fg_address), .in1(cpu_address), .out(multiplexer_2_out), .sel(and_1_out));
  Multiplexer #(.width(32)) multiplexer_3 (
    .in0(color_bg_address), .in1(cpu_address), .out(multiplexer_3_out), .sel(and_1_out));
  Multiplexer #(.width(32)) multiplexer_4 (
    .in0(character_rom_address), .in1(cpu_address), .out(multiplexer_4_out), .sel(and_1_out));
  // RAM #(.addrWidth(20), .clearpin("true"), .enables("line"), .line("quad"), .misaligned("true"), .trigger("falling"), .\type ("nonvolatile")) ram_1: pin names not known; wires that end beside it: and_1_out, 1'b1, or_1_out, data_type[1], data_type[1], ram_clk_gen_1_ram_clk, reset, ram_1_p8, ram_1_p9, ram_1_p10, ram_1_p11
  // RAM #(.addrWidth(20), .clearpin("true"), .enables("line"), .line("quad"), .misaligned("true"), .trigger("falling"), .\type ("nonvolatile")) ram_2: pin names not known; wires that end beside it: and_1_out, 1'b1, or_1_out, data_type[1], data_type[1], ram_clk_gen_1_ram_clk, reset, ram_2_p8, ram_2_p9, ram_2_p10, ram_2_p11
  // RAM #(.addrWidth(20), .clearpin("true"), .enables("line"), .line("quad"), .misaligned("true"), .trigger("falling"), .\type ("nonvolatile")) ram_3: pin names not known; wires that end beside it: and_1_out, 1'b1, or_1_out, data_type[1], data_type[1], ram_clk_gen_1_ram_clk, reset, ram_3_p8, ram_3_p9, ram_3_p10, ram_3_p11
  // RAM #(.addrWidth(20), .clearpin("true"), .enables("line"), .line("quad"), .misaligned("true"), .trigger("falling"), .\type ("nonvolatile")) ram_4: pin names not known; wires that end beside it: and_1_out, 1'b1, or_1_out, data_type[1], data_type[1], ram_clk_gen_1_ram_clk, reset, ram_4_p8, ram_4_p9, ram_4_p10, ram_4_p11
  not not_1 (not_1_out, and_1_out);
  Register #(.trigger("falling"), .width(32)) register_1 (
    .D({ram_1_p11, ram_1_p10, ram_1_p9, ram_1_p8}), .en(not_1_out), .clk(ram_clk_gen_1_ram_clk),
    .Q(vga_data_out), .clr(reset));
  Register #(.trigger("falling"), .width(32)) register_2 (
    .D({ram_2_p11, ram_2_p10, ram_2_p9, ram_2_p8}), .en(not_1_out), .clk(ram_clk_gen_1_ram_clk),
    .Q(color_fg_out), .clr(reset));
  Register #(.trigger("falling"), .width(32)) register_3 (
    .D({ram_3_p11, ram_3_p10, ram_3_p9, ram_3_p8}), .en(not_1_out), .clk(ram_clk_gen_1_ram_clk),
    .Q(color_bg_out), .clr(reset));
  Register #(.trigger("falling"), .width(32)) register_4 (
    .D({ram_4_p11, ram_4_p10, ram_4_p9, ram_4_p8}), .en(not_1_out), .clk(ram_clk_gen_1_ram_clk),
    .Q(character_data), .clr(reset));
endmodule
