// Logisim project riscv_core.circ as structural Verilog: 17 circuits, main circuit riscv_core
module riscv_core (
  input  irq,
  input  clk,
  input  reset,
  input  [31:0] data_in,
  output [31:0] data_out,
  output [1:0] data_type,
  output [31:0] address,
  output mem_rd,
  output mem_write
);

  wire and_1_out, and_2_out, branch_1_brnch, ex_mem_1_jump_branch_out, ex_mem_1_rf_we,
       forward_control_1_fw_en1, forward_control_1_fw_en2, hazard_control_1_address_src,
       hazard_control_1_flush, hazard_control_1_pc_en, id_ex_1_alu_src_1, id_ex_1_alu_src_2, id_ex_1_branch,
       id_ex_1_jump, if_id_1_clk_out, irq_control_1_insert_nop, irq_control_1_pc_stop, mem_wb_1_rf_we,
       not_1_out, or_1_out;
  wire [1:0] id_ex_1_alu_op, mem_wb_1_rf_src;
  wire [2:0] id_ex_1_funct3;
  wire [2:2] ex_mem_1_funct3_out;
  wire [4:0] ex_mem_1_reg_dest_out, id_ex_1_reg_dest, id_ex_1_rs1, id_ex_1_rs2, if_id_1_rs1, if_id_1_rs2,
       mem_wb_1_reg_dest_out;
  wire [6:0] id_ex_1_funct7;
  wire [10:0] control_logic_1_control_word, ex_mem_1_control_word_out, id_ex_1_control_word_out;
  wire [31:0] alu_1_result, alu_src_1_to_alu, alu_src_1_to_branch, alu_src_2_to_alu, alu_src_2_to_branch,
       ex_mem_1_alu_result_out, ex_mem_1_pc4_out, forward_control_1_fw_data1, forward_control_1_fw_data2,
       id_ex_1_immediate_out, id_ex_1_pc4_out, id_ex_1_pc_out, id_ex_1_reg_a_out, id_ex_1_reg_b_out,
       if_id_1_instruction_out, if_id_1_pc4_out, if_id_1_pc_out, imm_decode_1_immediate,
       irq_control_1_instruction_out, mem_align_1_data_aligned, mem_wb_1_alu_result_out, mem_wb_1_memory_out,
       mem_wb_1_pc4_out, multiplexer_1_out, multiplexer_2_out, multiplexer_3_out, multiplexer_4_out,
       program_ctr_1_pc, program_ctr_1_pc4, registers_1_a, registers_1_b;

  assign address = 1'b1 ? multiplexer_1_out : 32'bz;  // Controlled_Buffer controlled_buffer_1
  irq_control irq_control_1 (
    .irq_in(irq), .reset(reset), .clk(clk), .insert_nop(irq_control_1_insert_nop),
    .instruction_out(irq_control_1_instruction_out), .pc_stop(irq_control_1_pc_stop));
  Multiplexer #(.width(32)) multiplexer_1 (
    .in0(program_ctr_1_pc), .in1(ex_mem_1_alu_result_out), .out(multiplexer_1_out),
    .sel(hazard_control_1_address_src));
  program_ctr program_ctr_1 (
    .PC_src(or_1_out), .PC_en(hazard_control_1_pc_en), .clk(clk), .PC_in(alu_1_result), .reset(reset),
    .irq(irq_control_1_pc_stop), .PC(program_ctr_1_pc), .PC4(program_ctr_1_pc4));
  Multiplexer #(.width(32)) multiplexer_2 (
    .in0(data_in), .in1(irq_control_1_instruction_out), .out(multiplexer_2_out), .sel(irq_control_1_pc_stop));
  and and_1 (and_1_out, ~irq_control_1_insert_nop, hazard_control_1_pc_en);  // AND_Gate
  if_id if_id_1 (
    .PC_en(and_1_out), .clk(clk), .reset(hazard_control_1_flush), .PC(program_ctr_1_pc),
    .PC4(program_ctr_1_pc4), .instruction(multiplexer_2_out), .clk_out(if_id_1_clk_out),
    .PC_out(if_id_1_pc_out), .PC4_out(if_id_1_pc4_out), .instruction_out(if_id_1_instruction_out),
    .rs1(if_id_1_rs1), .rs2(if_id_1_rs2));
  registers registers_1 (
    .rd(mem_wb_1_reg_dest_out), .we(mem_wb_1_rf_we), .rs1(if_id_1_rs1), .rs2(if_id_1_rs2),
    .data(multiplexer_4_out), .clk(if_id_1_clk_out), .reset(reset), .b(registers_1_b), .a(registers_1_a));
  imm_decode imm_decode_1 (.instruction(if_id_1_instruction_out), .immediate(imm_decode_1_immediate));
  control_logic control_logic_1 (.opcode(if_id_1_instruction_out[6:0]), .control_word(control_logic_1_control_word));
  id_ex id_ex_1 (
    .clk(clk), .reset(hazard_control_1_flush), .control_word(control_logic_1_control_word),
    .reg_b(registers_1_b), .instruction(if_id_1_instruction_out), .PC(if_id_1_pc_out), .PC4(if_id_1_pc4_out),
    .immediate(imm_decode_1_immediate), .reg_a(registers_1_a), .reg_b_out(id_ex_1_reg_b_out),
    .PC_out(id_ex_1_pc_out), .PC4_out(id_ex_1_pc4_out), .immediate_out(id_ex_1_immediate_out),
    .reg_a_out(id_ex_1_reg_a_out), .control_word_out(id_ex_1_control_word_out), .jump(id_ex_1_jump),
    .branch(id_ex_1_branch), .alu_op(id_ex_1_alu_op), .alu_src_1(id_ex_1_alu_src_1),
    .alu_src_2(id_ex_1_alu_src_2), .reg_dest(id_ex_1_reg_dest), .funct3(id_ex_1_funct3), .rs1(id_ex_1_rs1),
    .rs2(id_ex_1_rs2), .funct7(id_ex_1_funct7));
  alu_src alu_src_1 (
    .sel_reg(id_ex_1_alu_src_1), .sel_forward(forward_control_1_fw_en1), .reg_data(id_ex_1_reg_a_out),
    .fw_data(forward_control_1_fw_data1), .opt_data(id_ex_1_pc_out), .to_branch(alu_src_1_to_branch),
    .to_alu(alu_src_1_to_alu));
  alu_src alu_src_2 (
    .sel_reg(id_ex_1_alu_src_2), .sel_forward(forward_control_1_fw_en2), .reg_data(id_ex_1_reg_b_out),
    .fw_data(forward_control_1_fw_data2), .opt_data(id_ex_1_immediate_out), .to_branch(alu_src_2_to_branch),
    .to_alu(alu_src_2_to_alu));
  forward_control forward_control_1 (
    .wb_reg_dest(mem_wb_1_reg_dest_out), .rs1(id_ex_1_rs1), .mem_reg_dest(ex_mem_1_reg_dest_out),
    .rs2(id_ex_1_rs2), .mem_reg_write(ex_mem_1_rf_we), .wb_reg_write(mem_wb_1_rf_we),
    .data_wb(multiplexer_4_out), .data_mem(multiplexer_3_out), .fw_data1(forward_control_1_fw_data1),
    .fw_data2(forward_control_1_fw_data2), .fw_en1(forward_control_1_fw_en1),
    .fw_en2(forward_control_1_fw_en2));
  and and_2 (and_2_out, id_ex_1_branch, branch_1_brnch);
  branch branch_1 (.funct3(id_ex_1_funct3), .a(alu_src_1_to_branch), .b(alu_src_2_to_branch), .brnch(branch_1_brnch));
  alu alu_1 (
    .alu_op(id_ex_1_alu_op), .funct3(id_ex_1_funct3), .A(alu_src_1_to_alu), .B(alu_src_2_to_alu),
    .funct7(id_ex_1_funct7), .result(alu_1_result));
  or or_1 (or_1_out, id_ex_1_jump, and_2_out);
  ex_mem ex_mem_1 (
    .jump_branch(or_1_out), .clk(clk), .reset(reset), .reg_dest(id_ex_1_reg_dest),
    .control_word(id_ex_1_control_word_out), .funct3(id_ex_1_funct3), .reg_b(alu_src_2_to_branch),
    .PC4(id_ex_1_pc4_out), .alu_result(alu_1_result), .funct3_out({ex_mem_1_funct3_out[2], data_type}),
    .reg_b_out(data_out), .reg_dest_out(ex_mem_1_reg_dest_out), .PC4_out(ex_mem_1_pc4_out),
    .control_word_out(ex_mem_1_control_word_out), .mem_read(mem_rd), .mem_write(mem_write),
    .rf_we(ex_mem_1_rf_we), .jump_branch_out(ex_mem_1_jump_branch_out),
    .alu_result_out(ex_mem_1_alu_result_out));
  hazard_control hazard_control_1 (
    .reset(reset), .jump_branch_ex(or_1_out), .clk(clk), .jump_branch_mem(ex_mem_1_jump_branch_out),
    .mem_read(mem_rd), .mem_write(mem_write), .PC_en(hazard_control_1_pc_en),
    .address_src(hazard_control_1_address_src), .flush(hazard_control_1_flush));
  mem_align mem_align_1 (
    .funct3({ex_mem_1_funct3_out[2], data_type}), .data(data_in), .data_aligned(mem_align_1_data_aligned));
  Multiplexer #(.width(32)) multiplexer_3 (
    .in0(mem_align_1_data_aligned), .in1(ex_mem_1_alu_result_out), .out(multiplexer_3_out), .sel(not_1_out));
  not not_1 (not_1_out, mem_rd);
  mem_wb mem_wb_1 (
    .clk(clk), .reset(reset), .reg_dest(ex_mem_1_reg_dest_out), .control_word(ex_mem_1_control_word_out),
    .alu_result(ex_mem_1_alu_result_out), .PC4(ex_mem_1_pc4_out), .memory(mem_align_1_data_aligned),
    .alu_result_out(mem_wb_1_alu_result_out), .PC4_out(mem_wb_1_pc4_out), .memory_out(mem_wb_1_memory_out),
    .reg_dest_out(mem_wb_1_reg_dest_out), .rf_src(mem_wb_1_rf_src), .rf_we(mem_wb_1_rf_we));
  Multiplexer #(.select(2), .width(32)) multiplexer_4 (
    .in0(mem_wb_1_memory_out), .in1(mem_wb_1_pc4_out), .in2(mem_wb_1_alu_result_out), .in3({32{1'b0}}),
    .out(multiplexer_4_out), .sel(mem_wb_1_rf_src));
endmodule

module alu (
  input  [31:0] A,
  input  [31:0] B,
  input  [1:0] alu_op,
  input  [6:0] funct7,
  input  [2:0] funct3,
  output [31:0] result
);

  wire alu_control_1_bypass, alu_control_1_funct3_en, alu_control_1_inv, comparator_1_lt, comparator_2_lt;
  wire [2:0] multiplexer_1_out;
  wire [3:3] alu_control_1_m_en;
  wire [31:0] adder_1_out, and_1_out, bit_extender_7_out, bit_extender_8_out, divider_1_out, divider_1_rem,
       divider_2_out, divider_2_rem, multiplexer_2_out, multiplexer_3_out, multiplexer_4_out,
       multiplier_1_out, or_1_out, shifter_1_out, shifter_2_out, shifter_3_out, subtractor_1_out, xor_1_out;
  wire [63:0] bit_extender_1_out, bit_extender_2_out, bit_extender_3_out, bit_extender_4_out,
       bit_extender_5_out, bit_extender_6_out, multiplier_2_out, multiplier_3_out, multiplier_4_out;

  Multiplexer #(.width(3)) multiplexer_1 (
    .in0(3'b000), .in1(funct3), .out(multiplexer_1_out), .sel(alu_control_1_funct3_en));
  alu_control alu_control_1 (
    .alu_op(alu_op), .funct7(funct7), .inv(alu_control_1_inv), .M_en(alu_control_1_m_en[3]),
    .funct3_en(alu_control_1_funct3_en), .bypass(alu_control_1_bypass));
  Adder #(.width(32)) adder_1 (.a(A), .b(B), .out(adder_1_out));  // open: cin, cout
  Subtractor #(.width(32)) subtractor_1 (.a(A), .b(B), .out(subtractor_1_out));  // open: bin, bout
  Shifter #(.width(32)) shifter_1 (.in(A), .\dist (B[4:0]), .out(shifter_1_out));
  Comparator #(.width(32)) comparator_1 (.a(A), .b(B), .lt(comparator_1_lt));  // open: gt, eq
  Comparator #(.mode("unsigned"), .width(32)) comparator_2 (.a(A), .b(B), .lt(comparator_2_lt));  // open: gt, eq
  assign xor_1_out = A ^ B;  // XOR_Gate xor_1, 32 bits wide
  Shifter #(.shift("lr"), .width(32)) shifter_2 (.in(A), .\dist (B[4:0]), .out(shifter_2_out));
  Shifter #(.shift("ar"), .width(32)) shifter_3 (.in(A), .\dist (B[4:0]), .out(shifter_3_out));
  assign or_1_out = A | B;  // OR_Gate or_1, 32 bits wide
  assign and_1_out = A & B;  // AND_Gate and_1, 32 bits wide
  Multiplier #(.width(32)) multiplier_1 (.a(A), .b(B), .out(multiplier_1_out));  // open: cin, cout
  assign bit_extender_1_out = {{32{A[31]}}, A};  // Bit_Extender bit_extender_1
  assign bit_extender_2_out = {{32{B[31]}}, B};  // Bit_Extender bit_extender_2
  assign bit_extender_3_out = {{32{A[31]}}, A};  // Bit_Extender bit_extender_3
  assign bit_extender_4_out = {{32{1'b0}}, B};  // Bit_Extender bit_extender_4
  assign bit_extender_5_out = {{32{1'b0}}, A};  // Bit_Extender bit_extender_5
  assign bit_extender_6_out = {{32{1'b0}}, B};  // Bit_Extender bit_extender_6
  Divider #(.mode("twosComplement"), .width(32)) divider_1 (
    .a(A), .b(B), .out(divider_1_out), .rem(divider_1_rem));  // open: upper
  Divider #(.width(32)) divider_2 (.a(A), .b(B), .out(divider_2_out), .rem(divider_2_rem));  // open: upper
  Multiplexer #(.width(32)) multiplexer_2 (
    .in0(adder_1_out), .in1(subtractor_1_out), .out(multiplexer_2_out), .sel(alu_control_1_inv));
  assign bit_extender_7_out = {{31{1'b0}}, comparator_1_lt};  // Bit_Extender bit_extender_7
  assign bit_extender_8_out = {{31{1'b0}}, comparator_2_lt};  // Bit_Extender bit_extender_8
  Multiplexer #(.width(32)) multiplexer_3 (
    .in0(shifter_2_out), .in1(shifter_3_out), .out(multiplexer_3_out), .sel(alu_control_1_inv));
  Multiplier #(.width(64)) multiplier_2 (
    .a(bit_extender_1_out), .b(bit_extender_2_out), .out(multiplier_2_out));  // open: cin, cout
  Multiplier #(.width(64)) multiplier_3 (
    .a(bit_extender_3_out), .b(bit_extender_4_out), .out(multiplier_3_out));  // open: cin, cout
  Multiplier #(.width(64)) multiplier_4 (
    .a(bit_extender_5_out), .b(bit_extender_6_out), .out(multiplier_4_out));  // open: cin, cout
  Multiplexer #(.select(4), .width(32)) multiplexer_4 (
    .in0(multiplexer_2_out), .in1(shifter_1_out), .in2(bit_extender_7_out), .in3(bit_extender_8_out),
    .in4(xor_1_out), .in5(multiplexer_3_out), .in6(or_1_out), .in7(and_1_out), .in8(multiplier_1_out),
    .in9(multiplier_2_out[63:32]), .in10(multiplier_3_out[63:32]), .in11(multiplier_4_out[63:32]),
    .in12(divider_1_out), .in13(divider_2_out), .in14(divider_1_rem), .in15(divider_2_rem),
    .out(multiplexer_4_out), .sel({alu_control_1_m_en[3], multiplexer_1_out}));
  Multiplexer #(.width(32)) multiplexer_5 (.in0(multiplexer_4_out), .in1(B), .out(result), .sel(alu_control_1_bypass));

  // Notes on the sheet:
  //   ADD
  //   SUB
  //   SLL
  //   SLT
  //   SLTU
  //   XOR
  //   SRL
  //   SRA
  //   OR
  //   AND
  //   MUL
  //   MULH
  //   MULHSU
  //   MULHU
  //   DIV/REM
  //   DIVU/REMU
endmodule

module if_id (
  input  [31:0] PC,
  input  [31:0] PC4,
  input  PC_en,
  input  [31:0] instruction,
  input  clk,
  input  reset,
  output [31:0] PC_out,
  output [31:0] PC4_out,
  output [31:0] instruction_out,
  output [4:0] rs1,
  output [4:0] rs2,
  output clk_out
);

  wire [31:0] multiplexer_1_out;

  Register #(.width(32)) register_1 (.D(PC), .clk(clk), .Q(PC_out), .clr(reset));  // open: en
  Register #(.width(32)) register_2 (.D(PC4), .clk(clk), .Q(PC4_out), .clr(reset));  // open: en
  Register #(.width(32)) register_3 (.D(multiplexer_1_out), .clk(clk), .Q(instruction_out), .clr(reset));  // open: en
  Multiplexer #(.width(32)) multiplexer_1 (.in0(32'h13), .in1(instruction), .out(multiplexer_1_out), .sel(PC_en));

  assign clk_out = clk;
  assign rs1 = instruction_out[19:15];
  assign rs2 = instruction_out[24:20];
endmodule

module id_ex (
  input  [31:0] reg_a,
  input  [31:0] reg_b,
  input  [31:0] instruction,
  input  [31:0] PC,
  input  [31:0] PC4,
  input  [31:0] immediate,
  input  [10:0] control_word,
  input  clk,
  input  reset,
  output [31:0] reg_a_out,
  output [31:0] reg_b_out,
  output [4:0] reg_dest,
  output [2:0] funct3,
  output [4:0] rs1,
  output [4:0] rs2,
  output [6:0] funct7,
  output [31:0] PC_out,
  output [31:0] PC4_out,
  output [31:0] immediate_out,
  output [10:0] control_word_out,
  output jump,
  output branch,
  output [1:0] alu_op,
  output alu_src_1,
  output alu_src_2
);

  wire [6:0] register_3_q;

  Register #(.width(32)) register_1 (.D(reg_a), .clk(clk), .Q(reg_a_out), .clr(reset));  // open: en
  Register #(.width(32)) register_2 (.D(reg_b), .clk(clk), .Q(reg_b_out), .clr(reset));  // open: en
  Register #(.width(32)) register_3 (
    .D(instruction), .clk(clk), .Q({funct7, rs2, rs1, funct3, reg_dest, register_3_q}), .clr(reset));  // open: en
  Register #(.width(32)) register_4 (.D(PC), .clk(clk), .Q(PC_out), .clr(reset));  // open: en
  Register #(.width(32)) register_5 (.D(PC4), .clk(clk), .Q(PC4_out), .clr(reset));  // open: en
  Register #(.width(32)) register_6 (.D(immediate), .clk(clk), .Q(immediate_out), .clr(reset));  // open: en
  Register #(.width(11)) register_7 (
    .D(control_word), .clk(clk),
    .Q({control_word_out[10:9], alu_src_2, alu_src_1, alu_op, control_word_out[4:2], branch, control_word_out[0]}),
    .clr(reset));  // open: en

  assign {control_word_out[8:5], control_word_out[1]} = {alu_src_2, alu_src_1, alu_op, branch};
  assign jump = control_word_out[0];
endmodule

module ex_mem (
  input  [31:0] alu_result,
  input  [2:0] funct3,
  input  [31:0] reg_b,
  input  [4:0] reg_dest,
  input  [31:0] PC4,
  input  [10:0] control_word,
  input  jump_branch,
  input  clk,
  input  reset,
  output [31:0] alu_result_out,
  output [2:0] funct3_out,
  output [31:0] reg_b_out,
  output [4:0] reg_dest_out,
  output [31:0] PC4_out,
  output [10:0] control_word_out,
  output mem_read,
  output mem_write,
  output rf_we,
  output jump_branch_out
);

  Register #(.width(32)) register_1 (.D(alu_result), .clk(clk), .Q(alu_result_out), .clr(reset));  // open: en
  Register #(.width(3)) register_2 (.D(funct3), .clk(clk), .Q(funct3_out), .clr(reset));  // open: en
  Register #(.width(32)) register_3 (.D(reg_b), .clk(clk), .Q(reg_b_out), .clr(reset));  // open: en
  Register #(.width(5)) register_4 (.D(reg_dest), .clk(clk), .Q(reg_dest_out), .clr(reset));  // open: en
  Register #(.width(32)) register_5 (.D(PC4), .clk(clk), .Q(PC4_out), .clr(reset));  // open: en
  Register #(.width(11)) register_6 (.D(control_word), .clk(clk), .Q(control_word_out), .clr(reset));  // open: en
  Register #(.width(1)) register_7 (.D(jump_branch), .clk(clk), .Q(jump_branch_out), .clr(reset));  // open: en

  assign mem_read = control_word_out[9];
  assign mem_write = control_word_out[10];
  assign rf_we = control_word_out[4];
endmodule

module mem_wb (
  input  [31:0] alu_result,
  input  [31:0] PC4,
  input  [31:0] memory,
  input  [4:0] reg_dest,
  input  [10:0] control_word,
  input  clk,
  input  reset,
  output [31:0] alu_result_out,
  output [31:0] PC4_out,
  output [31:0] memory_out,
  output [4:0] reg_dest_out,
  output [1:0] rf_src,
  output rf_we
);

  wire [10:0] register_5_q;

  Register #(.width(32)) register_1 (.D(alu_result), .clk(clk), .Q(alu_result_out), .clr(reset));  // open: en
  Register #(.width(32)) register_2 (.D(PC4), .clk(clk), .Q(PC4_out), .clr(reset));  // open: en
  Register #(.width(32)) register_3 (.D(memory), .clk(clk), .Q(memory_out), .clr(reset));  // open: en
  Register #(.width(5)) register_4 (.D(reg_dest), .clk(clk), .Q(reg_dest_out), .clr(reset));  // open: en
  Register #(.width(11)) register_5 (
    .D(control_word), .clk(clk), .Q({register_5_q[10:5], rf_we, rf_src, register_5_q[1:0]}), .clr(reset));  // open: en
endmodule

module registers (
  input  [31:0] data,
  input  clk,
  input  [4:0] rs1,
  input  reset,
  input  [4:0] rs2,
  input  [4:0] rd,
  input  we,
  output [31:0] a,
  output [31:0] b
);

  wire [31:0] decoder_1_out0, register_1_q, register_2_q, register_3_q, register_4_q, register_5_q,
       register_6_q, register_7_q, register_8_q, register_9_q, register_10_q, register_11_q, register_12_q,
       register_13_q, register_14_q, register_15_q, register_16_q, register_17_q, register_18_q,
       register_19_q, register_20_q, register_21_q, register_22_q, register_23_q, register_24_q,
       register_25_q, register_26_q, register_27_q, register_28_q, register_29_q, register_30_q,
       register_31_q;

  Decoder #(.select(5)) decoder_1 (
    .out0(decoder_1_out0[0]), .out1(decoder_1_out0[1]), .out2(decoder_1_out0[2]), .out3(decoder_1_out0[3]),
    .out4(decoder_1_out0[4]), .out5(decoder_1_out0[5]), .out6(decoder_1_out0[6]), .out7(decoder_1_out0[7]),
    .out8(decoder_1_out0[8]), .out9(decoder_1_out0[9]), .out10(decoder_1_out0[10]),
    .out11(decoder_1_out0[11]), .out12(decoder_1_out0[12]), .out13(decoder_1_out0[13]),
    .out14(decoder_1_out0[14]), .out15(decoder_1_out0[15]), .out16(decoder_1_out0[16]),
    .out17(decoder_1_out0[17]), .out18(decoder_1_out0[18]), .out19(decoder_1_out0[19]),
    .out20(decoder_1_out0[20]), .out21(decoder_1_out0[21]), .out22(decoder_1_out0[22]),
    .out23(decoder_1_out0[23]), .out24(decoder_1_out0[24]), .out25(decoder_1_out0[25]),
    .out26(decoder_1_out0[26]), .out27(decoder_1_out0[27]), .out28(decoder_1_out0[28]),
    .out29(decoder_1_out0[29]), .out30(decoder_1_out0[30]), .out31(decoder_1_out0[31]), .sel(rd), .en(we));
  Register #(.trigger("falling"), .width(32)) register_1 (
    .D(data), .en(decoder_1_out0[8]), .clk(clk), .Q(register_1_q), .clr(reset));
  Register #(.trigger("falling"), .width(32)) register_2 (
    .D(data), .en(decoder_1_out0[16]), .clk(clk), .Q(register_2_q), .clr(reset));
  Register #(.trigger("falling"), .width(32)) register_3 (
    .D(data), .en(decoder_1_out0[24]), .clk(clk), .Q(register_3_q), .clr(reset));
  Register #(.trigger("falling"), .width(32)) register_4 (
    .D(data), .en(decoder_1_out0[1]), .clk(clk), .Q(register_4_q), .clr(reset));
  Register #(.trigger("falling"), .width(32)) register_5 (
    .D(data), .en(decoder_1_out0[9]), .clk(clk), .Q(register_5_q), .clr(reset));
  Register #(.trigger("falling"), .width(32)) register_6 (
    .D(data), .en(decoder_1_out0[17]), .clk(clk), .Q(register_6_q), .clr(reset));
  Register #(.trigger("falling"), .width(32)) register_7 (
    .D(data), .en(decoder_1_out0[25]), .clk(clk), .Q(register_7_q), .clr(reset));
  Register #(.trigger("falling"), .width(32)) register_8 (
    .D(data), .en(decoder_1_out0[2]), .clk(clk), .Q(register_8_q), .clr(reset));
  Register #(.trigger("falling"), .width(32)) register_9 (
    .D(data), .en(decoder_1_out0[10]), .clk(clk), .Q(register_9_q), .clr(reset));
  Register #(.trigger("falling"), .width(32)) register_10 (
    .D(data), .en(decoder_1_out0[18]), .clk(clk), .Q(register_10_q), .clr(reset));
  Register #(.trigger("falling"), .width(32)) register_11 (
    .D(data), .en(decoder_1_out0[26]), .clk(clk), .Q(register_11_q), .clr(reset));
  Register #(.trigger("falling"), .width(32)) register_12 (
    .D(data), .en(decoder_1_out0[3]), .clk(clk), .Q(register_12_q), .clr(reset));
  Register #(.trigger("falling"), .width(32)) register_13 (
    .D(data), .en(decoder_1_out0[11]), .clk(clk), .Q(register_13_q), .clr(reset));
  Register #(.trigger("falling"), .width(32)) register_14 (
    .D(data), .en(decoder_1_out0[19]), .clk(clk), .Q(register_14_q), .clr(reset));
  Register #(.trigger("falling"), .width(32)) register_15 (
    .D(data), .en(decoder_1_out0[27]), .clk(clk), .Q(register_15_q), .clr(reset));
  Register #(.trigger("falling"), .width(32)) register_16 (
    .D(data), .en(decoder_1_out0[4]), .clk(clk), .Q(register_16_q), .clr(reset));
  Register #(.trigger("falling"), .width(32)) register_17 (
    .D(data), .en(decoder_1_out0[12]), .clk(clk), .Q(register_17_q), .clr(reset));
  Register #(.trigger("falling"), .width(32)) register_18 (
    .D(data), .en(decoder_1_out0[20]), .clk(clk), .Q(register_18_q), .clr(reset));
  Register #(.trigger("falling"), .width(32)) register_19 (
    .D(data), .en(decoder_1_out0[28]), .clk(clk), .Q(register_19_q), .clr(reset));
  Register #(.trigger("falling"), .width(32)) register_20 (
    .D(data), .en(decoder_1_out0[5]), .clk(clk), .Q(register_20_q), .clr(reset));
  Register #(.trigger("falling"), .width(32)) register_21 (
    .D(data), .en(decoder_1_out0[13]), .clk(clk), .Q(register_21_q), .clr(reset));
  Register #(.trigger("falling"), .width(32)) register_22 (
    .D(data), .en(decoder_1_out0[21]), .clk(clk), .Q(register_22_q), .clr(reset));
  Register #(.trigger("falling"), .width(32)) register_23 (
    .D(data), .en(decoder_1_out0[29]), .clk(clk), .Q(register_23_q), .clr(reset));
  Register #(.trigger("falling"), .width(32)) register_24 (
    .D(data), .en(decoder_1_out0[6]), .clk(clk), .Q(register_24_q), .clr(reset));
  Register #(.trigger("falling"), .width(32)) register_25 (
    .D(data), .en(decoder_1_out0[14]), .clk(clk), .Q(register_25_q), .clr(reset));
  Register #(.trigger("falling"), .width(32)) register_26 (
    .D(data), .en(decoder_1_out0[22]), .clk(clk), .Q(register_26_q), .clr(reset));
  Register #(.trigger("falling"), .width(32)) register_27 (
    .D(data), .en(decoder_1_out0[30]), .clk(clk), .Q(register_27_q), .clr(reset));
  Register #(.trigger("falling"), .width(32)) register_28 (
    .D(data), .en(decoder_1_out0[7]), .clk(clk), .Q(register_28_q), .clr(reset));
  Register #(.trigger("falling"), .width(32)) register_29 (
    .D(data), .en(decoder_1_out0[15]), .clk(clk), .Q(register_29_q), .clr(reset));
  Register #(.trigger("falling"), .width(32)) register_30 (
    .D(data), .en(decoder_1_out0[23]), .clk(clk), .Q(register_30_q), .clr(reset));
  Register #(.trigger("falling"), .width(32)) register_31 (
    .D(data), .en(decoder_1_out0[31]), .clk(clk), .Q(register_31_q), .clr(reset));
  Multiplexer #(.select(5), .width(32)) multiplexer_1 (
    .in0({32{1'b0}}), .in1(register_4_q), .in2(register_8_q), .in3(register_12_q), .in4(register_16_q),
    .in5(register_20_q), .in6(register_24_q), .in7(register_28_q), .in8(register_1_q), .in9(register_5_q),
    .in10(register_9_q), .in11(register_13_q), .in12(register_17_q), .in13(register_21_q),
    .in14(register_25_q), .in15(register_29_q), .in16(register_2_q), .in17(register_6_q),
    .in18(register_10_q), .in19(register_14_q), .in20(register_18_q), .in21(register_22_q),
    .in22(register_26_q), .in23(register_30_q), .in24(register_3_q), .in25(register_7_q),
    .in26(register_11_q), .in27(register_15_q), .in28(register_19_q), .in29(register_23_q),
    .in30(register_27_q), .in31(register_31_q), .out(a), .sel(rs1));
  Multiplexer #(.select(5), .width(32)) multiplexer_2 (
    .in0({32{1'b0}}), .in1(register_4_q), .in2(register_8_q), .in3(register_12_q), .in4(register_16_q),
    .in5(register_20_q), .in6(register_24_q), .in7(register_28_q), .in8(register_1_q), .in9(register_5_q),
    .in10(register_9_q), .in11(register_13_q), .in12(register_17_q), .in13(register_21_q),
    .in14(register_25_q), .in15(register_29_q), .in16(register_2_q), .in17(register_6_q),
    .in18(register_10_q), .in19(register_14_q), .in20(register_18_q), .in21(register_22_q),
    .in22(register_26_q), .in23(register_30_q), .in24(register_3_q), .in25(register_7_q),
    .in26(register_11_q), .in27(register_15_q), .in28(register_19_q), .in29(register_23_q),
    .in30(register_27_q), .in31(register_31_q), .out(b), .sel(rs2));
endmodule

module alu_control (
  input  [1:0] alu_op,
  input  [6:0] funct7,
  output inv,
  output M_en,
  output funct3_en,
  output bypass
);

  wire [2:0] comparator_1_eq;

  Comparator #(.mode("unsigned"), .width(7)) comparator_1 (
    .a(funct7), .b({7{1'b0}}), .eq(comparator_1_eq[0]));  // open: gt, lt
  Comparator #(.mode("unsigned"), .width(7)) comparator_2 (
    .a(funct7), .b(7'b0100000), .eq(comparator_1_eq[1]));  // open: gt, lt
  Comparator #(.mode("unsigned"), .width(7)) comparator_3 (
    .a(funct7), .b(7'b0000001), .eq(comparator_1_eq[2]));  // open: gt, lt
  PLA #(.in_width(5), .out_width(4), .\table ("xxx00 0000 # ADD\n00101 0100 # R-TYPE\n01001 0101 # R-ALT\nxxx10 0100 # I-TYPE\n10001 0110 # M-EXT\nxxx11 1000 # BYPASS")) pla_1 (
    .in({comparator_1_eq, alu_op}), .out({bypass, funct3_en, M_en, inv}));

  // Notes on the sheet:
  //   R-TYPE
  //   INV FX
  //   M EXT
endmodule

module imm_decode (
  input  [31:0] instruction,
  output [31:0] immediate
);

  wire [2:0] pla_1_out;
  wire [11:0] bit_extender_4_out;
  wire [19:0] bit_extender_3_out;
  wire [26:0] bit_extender_2_out;
  wire [31:0] bit_extender_1_out;

  assign bit_extender_1_out = {{20{instruction[31]}}, instruction[31:20]};  // Bit_Extender bit_extender_1
  assign bit_extender_2_out = {{20{instruction[31]}}, instruction[31:25]};  // Bit_Extender bit_extender_2
  assign bit_extender_3_out = {{19{instruction[31]}}, instruction[31]};  // Bit_Extender bit_extender_3
  assign bit_extender_4_out = {{11{instruction[31]}}, instruction[31]};  // Bit_Extender bit_extender_4
  Multiplexer #(.select(3), .width(32)) multiplexer_1 (
    .in0(bit_extender_1_out), .in1({bit_extender_2_out, instruction[11:7]}),
    .in2({bit_extender_3_out, instruction[7], instruction[30:25], instruction[11:8], 1'b0}),
    .in3({instruction[31:12], {12{1'b0}}}),
    .in4({bit_extender_4_out, instruction[19:12], instruction[20], instruction[30:21], 1'b0}),
    .out(immediate), .sel(pla_1_out));  // open: in5, in6, in7
  PLA #(.in_width(5), .out_width(3), .\table ("00000 000 # I-LW\n11001 000 # I-JALR\n00100 000 # I-A\n01000 001 # S\n11000 010 # B\n01101 011 # U-LUI\n00101 011 # U-AUIPC\n01100 011 # U-R\n11011 100 # J")) pla_1 (
    .in(instruction[6:2]), .out(pla_1_out));

  // Notes on the sheet:
  //   I
  //   S
  //   B
  //   U
  //   J
endmodule

module control_logic (
  input  [6:0] opcode,
  output [10:0] control_word
);

  PLA #(.in_width(7), .out_width(11), .\table ("0110111 00101111000 # LUI\n0010111 00110011000 # AUIPC\n1101111 00110010101 # JAL\n1100111 00100010101 # JALR\n1100011 00110000010 # B--\n0000011 01100010000 # L-\n0100011 10100000000 # S-\n0010011 00101011000 # R-IMM\n0110011 00000111000 # R-TYPE")) pla_1 (
    .in(opcode), .out(control_word));
endmodule

module program_ctr (
  input  PC_src,
  input  [31:0] PC_in,
  input  PC_en,
  input  clk,
  input  reset,
  input  irq,
  output [31:0] PC,
  output [31:0] PC4
);

  wire [31:0] adder_1_out, and_1_out, multiplexer_1_out, multiplexer_2_out;

  assign and_1_out = PC_in & ~32'h1;  // AND_Gate and_1, 32 bits wide
  Register #(.width(32)) register_1 (.D(multiplexer_1_out), .en(PC_en), .clk(clk), .Q(PC), .clr(reset));
  Multiplexer #(.width(32)) multiplexer_1 (
    .in0(multiplexer_2_out), .in1(and_1_out), .out(multiplexer_1_out), .sel(PC_src));
  Multiplexer #(.width(32)) multiplexer_2 (.in0(adder_1_out), .in1(PC), .out(multiplexer_2_out), .sel(irq));
  Adder #(.width(32)) adder_1 (.a(PC), .b(32'h4), .out(adder_1_out));  // open: cin, cout
  Multiplexer #(.width(32)) multiplexer_3 (.in0(adder_1_out), .in1(PC), .out(PC4), .sel(irq));

  // Notes on the sheet:
  //   (make even)
endmodule

module branch (
  input  [31:0] a,
  input  [31:0] b,
  input  [2:0] funct3,
  output brnch
);

  wire comparator_1_eq, comparator_1_gt, comparator_1_lt, comparator_2_eq, comparator_2_gt, comparator_2_lt,
       not_1_out, or_1_out, or_2_out;

  Comparator #(.width(32)) comparator_1 (
    .a(a), .b(b), .gt(comparator_1_gt), .eq(comparator_1_eq), .lt(comparator_1_lt));
  Comparator #(.mode("unsigned"), .width(32)) comparator_2 (
    .a(a), .b(b), .gt(comparator_2_gt), .eq(comparator_2_eq), .lt(comparator_2_lt));
  or or_1 (or_1_out, comparator_1_gt, comparator_1_eq);
  not not_1 (not_1_out, comparator_1_eq);
  or or_2 (or_2_out, comparator_2_gt, comparator_2_eq);
  Multiplexer #(.select(3)) multiplexer_1 (
    .in0(comparator_1_eq), .in1(not_1_out), .in2(1'b0), .in3(1'b0), .in4(comparator_1_lt), .in5(or_1_out),
    .in6(comparator_2_lt), .in7(or_2_out), .out(brnch), .sel(funct3));
endmodule

module mem_align (
  input  [31:0] data,
  input  [2:0] funct3,
  output [31:0] data_aligned
);

  wire [31:0] bit_extender_1_out, bit_extender_2_out, bit_extender_3_out, bit_extender_4_out;

  assign bit_extender_1_out = {{24{data[7]}}, data[7:0]};  // Bit_Extender bit_extender_1
  assign bit_extender_2_out = {{16{data[15]}}, data[15:0]};  // Bit_Extender bit_extender_2
  assign bit_extender_3_out = {{24{1'b0}}, data[7:0]};  // Bit_Extender bit_extender_3
  assign bit_extender_4_out = {{16{1'b0}}, data[15:0]};  // Bit_Extender bit_extender_4
  Multiplexer #(.select(3), .width(32)) multiplexer_1 (
    .in0(bit_extender_1_out), .in1(bit_extender_2_out), .in2(data), .in3({32{1'b0}}),
    .in4(bit_extender_3_out), .in5(bit_extender_4_out), .in6({32{1'b0}}), .in7({32{1'b0}}),
    .out(data_aligned), .sel(funct3));

  // Notes on the sheet:
  //   LB
  //   LH
  //   LBU
  //   LHU
endmodule

module alu_src (
  input  [31:0] reg_data,
  input  [31:0] fw_data,
  input  [31:0] opt_data,
  input  sel_reg,
  input  sel_forward,
  output [31:0] to_branch,
  output [31:0] to_alu
);

  Multiplexer #(.width(32)) multiplexer_1 (.in0(reg_data), .in1(fw_data), .out(to_branch), .sel(sel_forward));
  Multiplexer #(.width(32)) multiplexer_2 (.in0(to_branch), .in1(opt_data), .out(to_alu), .sel(sel_reg));
endmodule

module hazard_control (
  input  reset,
  input  jump_branch_ex,
  input  clk,
  input  jump_branch_mem,
  input  mem_read,
  input  mem_write,
  output flush,
  output PC_en,
  output address_src
);

  wire d_ff_1_q;

  D_Flip_Flop d_ff_1 (.D(jump_branch_ex), .clk(clk), .Q(d_ff_1_q), .reset(jump_branch_mem));  // open: Qn, preset
  or or_1 (address_src, mem_read, mem_write);
  or or_2 (flush, reset, d_ff_1_q);
  or or_3 (PC_en, jump_branch_ex, ~address_src);  // OR_Gate
endmodule

module forward_control (
  input  [4:0] wb_reg_dest,
  input  [4:0] rs1,
  input  [4:0] mem_reg_dest,
  input  [4:0] rs2,
  input  mem_reg_write,
  input  wb_reg_write,
  input  [31:0] data_wb,
  input  [31:0] data_mem,
  output fw_en1,
  output fw_en2,
  output [31:0] fw_data1,
  output [31:0] fw_data2
);

  wire and_1_out, and_2_out, and_3_out, and_4_out, and_5_out, and_6_out, and_7_out, and_8_out,
       comparator_1_eq, comparator_2_eq, comparator_3_eq, comparator_4_eq, comparator_5_eq, comparator_6_eq,
       comparator_7_eq, comparator_8_eq;

  Comparator #(.mode("unsigned"), .width(5)) comparator_1 (
    .a(wb_reg_dest), .b(rs1), .eq(comparator_1_eq));  // open: gt, lt
  and and_1 (and_1_out, comparator_1_eq, ~comparator_2_eq);  // AND_Gate
  Comparator #(.mode("unsigned"), .width(5)) comparator_2 (
    .a(rs1), .b({5{1'b0}}), .eq(comparator_2_eq));  // open: gt, lt
  Comparator #(.mode("unsigned"), .width(5)) comparator_3 (
    .a(rs1), .b(mem_reg_dest), .eq(comparator_3_eq));  // open: gt, lt
  and and_2 (and_2_out, comparator_3_eq, ~comparator_4_eq);  // AND_Gate
  Comparator #(.mode("unsigned"), .width(5)) comparator_4 (
    .a(mem_reg_dest), .b({5{1'b0}}), .eq(comparator_4_eq));  // open: gt, lt
  Comparator #(.mode("unsigned"), .width(5)) comparator_5 (
    .a(rs2), .b(wb_reg_dest), .eq(comparator_5_eq));  // open: gt, lt
  and and_3 (and_3_out, comparator_5_eq, ~comparator_6_eq);  // AND_Gate
  Comparator #(.mode("unsigned"), .width(5)) comparator_6 (
    .a(wb_reg_dest), .b({5{1'b0}}), .eq(comparator_6_eq));  // open: gt, lt
  Comparator #(.mode("unsigned"), .width(5)) comparator_7 (
    .a(rs2), .b(mem_reg_dest), .eq(comparator_7_eq));  // open: gt, lt
  and and_4 (and_4_out, comparator_7_eq, ~comparator_8_eq);  // AND_Gate
  Comparator #(.mode("unsigned"), .width(5)) comparator_8 (
    .a(mem_reg_dest), .b({5{1'b0}}), .eq(comparator_8_eq));  // open: gt, lt
  and and_5 (and_5_out, and_1_out, wb_reg_write);
  and and_6 (and_6_out, and_2_out, mem_reg_write);
  and and_7 (and_7_out, and_3_out, wb_reg_write);
  and and_8 (and_8_out, and_4_out, mem_reg_write);
  Multiplexer #(.width(32)) multiplexer_1 (.in0(data_wb), .in1(data_mem), .out(fw_data1), .sel(and_6_out));
  Multiplexer #(.width(32)) multiplexer_2 (.in0(data_wb), .in1(data_mem), .out(fw_data2), .sel(and_8_out));
  or or_1 (fw_en1, and_5_out, and_6_out);
  or or_2 (fw_en2, and_7_out, and_8_out);
endmodule

module irq_control (
  input  irq_in,
  input  reset,
  input  clk,
  output insert_nop,
  output [31:0] instruction_out,
  output pc_stop
);

  wire and_2_out, and_3_out, counter_1_carry, counter_2_carry, or_1_out;

  Counter #(.max('h4), .ongoal("stay"), .width(3)) counter_1 (
    .clr(or_1_out), .load(1'b0), .up(1'b1), .count(irq_in), .clk(clk), .carry(counter_1_carry));  // open: D, Q
  or or_1 (or_1_out, ~irq_in, reset);  // OR_Gate
  Counter #(.max('h5), .ongoal("stay"), .width(3)) counter_2 (
    .clr(or_1_out), .load(1'b0), .up(1'b1), .count(irq_in), .clk(clk), .carry(counter_2_carry));  // open: D, Q
  and and_1 (insert_nop, irq_in, ~counter_1_carry);  // AND_Gate
  and and_2 (and_2_out, irq_in, ~counter_2_carry);  // AND_Gate
  and and_3 (and_3_out, ~insert_nop, and_2_out);  // AND_Gate
  or or_2 (pc_stop, insert_nop, and_2_out);
  assign instruction_out = and_3_out ? 32'h10000267 : 32'bz;  // Controlled_Buffer controlled_buffer_1
endmodule
