// Logisim project vga.circ as structural Verilog: 5 circuits, main circuit vga_counter
module vga_counter (
  input  clk,
  output [9:0] h_pos,
  output h_sync,
  output [9:0] v_pos,
  output v_sync
);

  wire comparator_1_eq, comparator_1_gt, comparator_2_lt, comparator_3_eq, comparator_3_gt, comparator_4_lt,
       counter_1_carry, counter_2_carry, or_1_out, or_2_out;
  wire [9:0] counter_2_q;

  Counter #(.max('h190), .ongoal("stay"), .width(10)) counter_1 (
    .clr(counter_1_carry), .load(1'b0), .up(1'b1), .clk(clk), .carry(counter_1_carry), .Q(h_pos));  // open: count, D
  Counter #(.max('h20d), .ongoal("stay"), .width(10)) counter_2 (
    .clr(counter_2_carry), .load(1'b0), .up(1'b1), .clk(counter_1_carry), .carry(counter_2_carry),
    .Q(counter_2_q));  // open: count, D
  Comparator #(.mode("unsigned"), .width(10)) comparator_1 (
    .a(h_pos), .b(10'h148), .gt(comparator_1_gt), .eq(comparator_1_eq));  // open: lt
  Comparator #(.mode("unsigned"), .width(10)) comparator_2 (
    .a(h_pos), .b(10'h178), .lt(comparator_2_lt));  // open: gt, eq
  Shifter #(.shift("lr"), .width(10)) shifter_1 (.in(counter_2_q), .\dist (4'b0001), .out(v_pos));
  Comparator #(.mode("unsigned"), .width(10)) comparator_3 (
    .a(counter_2_q), .b(10'h1ea), .gt(comparator_3_gt), .eq(comparator_3_eq));  // open: lt
  Comparator #(.mode("unsigned"), .width(10)) comparator_4 (
    .a(counter_2_q), .b(10'h1ec), .lt(comparator_4_lt));  // open: gt, eq
  or or_1 (or_1_out, comparator_1_gt, comparator_1_eq);
  nand nand_1 (h_sync, or_1_out, comparator_2_lt);
  or or_2 (or_2_out, comparator_3_gt, comparator_3_eq);
  nand nand_2 (v_sync, or_2_out, comparator_4_lt);
endmodule

module vga_control_reg (
  input  [31:0] data_in,
  input  vga_mode_en,
  input  vga_mem_en,
  input  color_ram_en,
  input  char_rom_en,
  input  clk,
  input  reset,
  output [7:0] vga_mode,
  output [31:0] vga_mem_location,
  output [31:0] color_ram_location,
  output [31:0] char_rom_location
);

  Register register_1 (.D(data_in[7:0]), .en(vga_mode_en), .clk(clk), .Q(vga_mode), .clr(reset));
  Register #(.width(32)) register_2 (.D(data_in), .en(vga_mem_en), .clk(clk), .Q(vga_mem_location), .clr(reset));
  Register #(.width(32)) register_3 (.D(data_in), .en(color_ram_en), .clk(clk), .Q(color_ram_location), .clr(reset));
  Register #(.width(32)) register_4 (.D(data_in), .en(char_rom_en), .clk(clk), .Q(char_rom_location), .clr(reset));
endmodule

module vga_output (
  input  [31:0] vga_mem_in,
  input  [31:0] character_rom_location,
  input  [31:0] color_bg_in,
  input  [31:0] color_fg_in,
  input  [31:0] character_rom_in,
  input  [7:0] vga_mode,
  input  [9:0] h_pos,
  input  [9:0] v_pos,
  input  [31:0] vga_mem_location,
  input  [31:0] color_ram_location,
  output [7:0] red,
  output [7:0] green,
  output [31:0] character_address,
  output [7:0] blue,
  output [31:0] vga_address,
  output [31:0] color_fg_address,
  output [31:0] color_bg_address
);

  wire comparator_1_gt;
  wire [10:0] shifter_1_out;
  wire [31:0] adder_1_out, adder_2_out, adder_3_out, adder_4_out, adder_5_out, adder_6_out, adder_8_out,
       bit_extender_1_out, bit_extender_2_out, bit_extender_3_out, multiplexer_3_out, multiplier_1_out,
       multiplier_2_out, multiplier_3_out, shifter_2_out, shifter_3_out, shifter_4_out, shifter_5_out,
       shifter_6_out, shifter_7_out;
  wire [31:24] multiplexer_4_out;

  assign bit_extender_1_out = {{22{1'b0}}, h_pos};  // Bit_Extender bit_extender_1
  assign bit_extender_2_out = {{22{1'b0}}, v_pos};  // Bit_Extender bit_extender_2
  assign bit_extender_3_out = {{21{1'b0}}, shifter_1_out};  // Bit_Extender bit_extender_3
  Shifter #(.width(11)) shifter_1 (.in(vga_mem_in[10:0]), .\dist (4'b0011), .out(shifter_1_out));
  Adder #(.width(32)) adder_1 (
    .a(bit_extender_3_out), .b(character_rom_location), .out(adder_1_out));  // open: cin, cout
  Comparator #(.mode("unsigned"), .width(3)) comparator_1 (
    .a(3'b100), .b(v_pos[2:0]), .gt(comparator_1_gt));  // open: eq, lt
  Shifter #(.shift("lr"), .width(32)) shifter_2 (.in(bit_extender_2_out), .\dist (5'b00011), .out(shifter_2_out));
  Shifter #(.width(32)) shifter_3 (.in(32'h8), .\dist (5'b00011), .out(shifter_3_out));
  Multiplexer #(.width(32)) multiplexer_1 (
    .in0(adder_1_out), .in1(adder_2_out), .out(character_address), .sel(comparator_1_gt));
  Adder #(.width(32)) adder_2 (.a(adder_1_out), .b(32'h4), .out(adder_2_out));  // open: cin, cout
  Shifter #(.width(32)) shifter_4 (.in(character_rom_in), .\dist ({v_pos[1:0], h_pos[2:0]}), .out(shifter_4_out));
  Shifter #(.width(32)) shifter_5 (.in(bit_extender_1_out), .\dist (5'b00010), .out(shifter_5_out));
  Multiplier #(.width(32)) multiplier_1 (
    .a(bit_extender_2_out), .b(32'h100), .out(multiplier_1_out));  // open: cin, cout
  Shifter #(.shift("lr"), .width(32)) shifter_6 (.in(bit_extender_1_out), .\dist (5'b00011), .out(shifter_6_out));
  Multiplier #(.width(32)) multiplier_2 (.a(shifter_2_out), .b(32'h8), .out(multiplier_2_out));  // open: cin, cout
  Adder #(.width(32)) adder_3 (.a(shifter_5_out), .b(multiplier_1_out), .out(adder_3_out));  // open: cin, cout
  Adder #(.width(32)) adder_4 (.a(adder_3_out), .b(vga_mem_location), .out(adder_4_out));  // open: cin, cout
  Adder #(.width(32)) adder_5 (.a(vga_mem_location), .b(adder_6_out), .out(adder_5_out));  // open: cin, cout
  Adder #(.width(32)) adder_6 (.a(shifter_6_out), .b(multiplier_2_out), .out(adder_6_out));  // open: cin, cout
  Shifter #(.width(32)) shifter_7 (.in(shifter_6_out), .\dist (5'b00011), .out(shifter_7_out));
  Multiplier #(.width(32)) multiplier_3 (
    .a(shifter_2_out), .b(shifter_3_out), .out(multiplier_3_out));  // open: cin, cout
  Multiplexer #(.width(32)) multiplexer_2 (.in0(adder_4_out), .in1(adder_5_out), .out(vga_address), .sel(vga_mode[0]));
  Adder #(.width(32)) adder_7 (.a(color_ram_location), .b(adder_8_out), .out(color_fg_address));  // open: cin, cout
  Adder #(.width(32)) adder_8 (.a(shifter_7_out), .b(multiplier_3_out), .out(adder_8_out));  // open: cin, cout
  Multiplexer #(.width(32)) multiplexer_3 (
    .in0(color_bg_in), .in1(color_fg_in), .out(multiplexer_3_out), .sel(shifter_4_out[31]));
  Adder #(.width(32)) adder_9 (.a(color_fg_address), .b(32'h4), .out(color_bg_address));  // open: cin, cout
  Multiplexer #(.width(32)) multiplexer_4 (
    .in0(vga_mem_in), .in1(multiplexer_3_out), .out({multiplexer_4_out, red, green, blue}), .sel(vga_mode[0]));

  // Notes on the sheet:
  //   Chars/Row
  //   # Rows x4
endmodule

module vga (
  input  [31:0] data_in,
  input  [31:0] cpu_address,
  input  write,
  input  ram_en,
  input  [1:0] data_type,
  input  clk,
  input  reset,
  input  ctrl_en,
  input  ctrl_read,
  output [9:0] v_pos,
  output [9:0] h_pos,
  output v_sync,
  output h_sync,
  output sys_clk,
  output [7:0] red,
  output [7:0] green,
  output [7:0] blue,
  output [31:0] ctrl_out
);

  wire and_1_out, and_2_out, decoder_1_out0, decoder_1_out1, decoder_1_out2, decoder_1_out3;
  wire [7:0] vga_control_reg_1_vga_mode;
  wire [31:0] multiplexer_1_out, vga_control_reg_1_char_rom_location, vga_control_reg_1_color_ram_location,
       vga_control_reg_1_vga_mem_location, vga_mem_1_character_data, vga_mem_1_color_bg_out,
       vga_mem_1_color_fg_out, vga_mem_1_vga_data_out, vga_output_1_character_address,
       vga_output_1_color_bg_address, vga_output_1_color_fg_address, vga_output_1_vga_address;
  wire [31:8] undriven;

  Decoder #(.select(2)) decoder_1 (
    .out0(decoder_1_out0), .out1(decoder_1_out1), .out2(decoder_1_out2), .out3(decoder_1_out3),
    .sel(cpu_address[3:2]), .en(and_1_out));
  and and_1 (and_1_out, write, ctrl_en);
  vga_counter_logisim vga_counter_logisim_1 (
    .clk(sys_clk), .reset(reset), .h_pos(h_pos), .h_sync(h_sync), .v_pos(v_pos), .v_sync(v_sync));
  vga_control_reg vga_control_reg_1 (
    .vga_mode_en(decoder_1_out0), .vga_mem_en(decoder_1_out1), .color_ram_en(decoder_1_out2),
    .char_rom_en(decoder_1_out3), .clk(sys_clk), .reset(reset), .data_in(data_in),
    .vga_mode(vga_control_reg_1_vga_mode), .vga_mem_location(vga_control_reg_1_vga_mem_location),
    .color_ram_location(vga_control_reg_1_color_ram_location),
    .char_rom_location(vga_control_reg_1_char_rom_location));
  Multiplexer #(.select(2), .width(32)) multiplexer_1 (
    .in0({undriven, vga_control_reg_1_vga_mode}), .in1(vga_control_reg_1_vga_mem_location),
    .in2(vga_control_reg_1_color_ram_location), .in3(vga_control_reg_1_char_rom_location),
    .out(multiplexer_1_out), .sel(cpu_address[3:2]));
  and and_2 (and_2_out, ctrl_en, ctrl_read);
  assign ctrl_out = and_2_out ? multiplexer_1_out : 32'bz;  // Controlled_Buffer controlled_buffer_1
  vga_output vga_output_1 (
    .vga_mode(vga_control_reg_1_vga_mode), .h_pos(h_pos), .v_pos(v_pos),
    .character_rom_in(vga_mem_1_character_data), .vga_mem_location(vga_control_reg_1_vga_mem_location),
    .color_ram_location(vga_control_reg_1_color_ram_location), .vga_mem_in(vga_mem_1_vga_data_out),
    .character_rom_location(vga_control_reg_1_char_rom_location), .color_bg_in(vga_mem_1_color_bg_out),
    .color_fg_in(vga_mem_1_color_fg_out), .red(red), .green(green), .blue(blue),
    .character_address(vga_output_1_character_address), .color_fg_address(vga_output_1_color_fg_address),
    .color_bg_address(vga_output_1_color_bg_address), .vga_address(vga_output_1_vga_address));
  vga_mem vga_mem_1 (
    .ram_write(write), .reset(reset), .clk(clk), .data_type(data_type), .data_in(data_in), .enable(ram_en),
    .character_rom_address(vga_output_1_character_address), .vga_address(vga_output_1_vga_address),
    .cpu_address(cpu_address), .color_fg_address(vga_output_1_color_fg_address),
    .color_bg_address(vga_output_1_color_bg_address), .color_bg_out(vga_mem_1_color_bg_out),
    .character_data(vga_mem_1_character_data), .vga_data_out(vga_mem_1_vga_data_out),
    .color_fg_out(vga_mem_1_color_fg_out), .sys_clk(sys_clk));
endmodule

module vga_counter_logisim (
  input  clk,
  input  reset,
  output [9:0] h_pos,
  output h_sync,
  output [9:0] v_pos,
  output v_sync
);

  wire comparator_1_eq, comparator_1_gt, comparator_2_lt, comparator_3_eq, comparator_3_gt, comparator_4_lt,
       counter_1_carry, counter_2_carry, or_1_out, or_2_out, or_3_out, or_4_out;
  wire [9:0] counter_2_q;

  Counter #(.max('h40), .ongoal("stay"), .width(10)) counter_1 (
    .clr(or_1_out), .load(1'b0), .up(1'b1), .clk(clk), .carry(counter_1_carry), .Q(h_pos));  // open: count, D
  Counter #(.max('h80), .ongoal("stay"), .width(10)) counter_2 (
    .clr(or_2_out), .load(1'b0), .up(1'b1), .clk(or_1_out), .carry(counter_2_carry), .Q(counter_2_q));  // open: count, D
  or or_1 (or_1_out, reset, counter_1_carry);
  or or_2 (or_2_out, reset, counter_2_carry);
  Comparator #(.mode("unsigned"), .width(10)) comparator_1 (
    .a(h_pos), .b(10'h148), .gt(comparator_1_gt), .eq(comparator_1_eq));  // open: lt
  Comparator #(.mode("unsigned"), .width(10)) comparator_2 (
    .a(h_pos), .b(10'h178), .lt(comparator_2_lt));  // open: gt, eq
  Shifter #(.shift("lr"), .width(10)) shifter_1 (.in(counter_2_q), .\dist (4'b0001), .out(v_pos));
  Comparator #(.mode("unsigned"), .width(10)) comparator_3 (
    .a(counter_2_q), .b(10'h1ea), .gt(comparator_3_gt), .eq(comparator_3_eq));  // open: lt
  Comparator #(.mode("unsigned"), .width(10)) comparator_4 (
    .a(counter_2_q), .b(10'h1ec), .lt(comparator_4_lt));  // open: gt, eq
  or or_3 (or_3_out, comparator_1_gt, comparator_1_eq);
  nand nand_1 (h_sync, or_3_out, comparator_2_lt);
  or or_4 (or_4_out, comparator_3_gt, comparator_3_eq);
  nand nand_2 (v_sync, or_4_out, comparator_4_lt);
endmodule
